# Fritzing sketch Spark.Core.MPL115A2 (saved by Fritzing 0.9.1b)
circuit board: 8.46667cm x 5.64444cm
breadboards: 1

parts:
  Spark_io_Core = Spark Core (v1.0)
  DHT22 = Humidity and Temperature Sensor RHT03
  MPL115A2 = MPL3115A2 [package=lga8]

nets:
  GND: Spark_io_Core.GND, DHT22.GND_2, MPL115A2.GND
  N1: Spark_io_Core.D0, MPL115A2.SDA
  N2: Spark_io_Core.D1, MPL115A2.SCL
  N3: Spark_io_Core.D4, DHT22.Data-signal
  3V3: Spark_io_Core.3V3, DHT22.Vcc, MPL115A2.VDD
